# Fritzing sketch tempSensor (saved by Fritzing 0.9.3b)
circuit board: 8.46667cm x 5.64444cm
perfboards: 4

parts:
  Raspberry_Pi_1 = Raspberry Pi 3 [part_number=RPI-3-V1.2]  # not connected
  J6 = female pin header, 3 pins [form="♀ (female)"]  # not connected
  J10 = female pin header, 3 pins [form="♀ (female)"]  # not connected
  J11 = female alternating pin header, 3 pins [form="♀ (female)"]  # not connected
  IC1 = IC, DIP package, 16 pins [chip_label=MCP3424]
  IC2 = IC, DIP package, 10 pins [chip_label=FCL100-1]
  IC3 = IC, DIP package, 10 pins [chip_label=FCL100-2]
  IC4 = IC, DIP package, 10 pins [chip_label=FCL100-3]
  IC5 = IC, DIP package, 10 pins [chip_label=FCL100-3]
  IC7 = IC, DIP package, 10 pins [chip_label=FCL100-3]
  IC8 = IC, DIP package, 10 pins [chip_label=FCL100-3]
  J12 = single row smd male pin header, 5 pins [form="♂ (male)"]
  J13 = single row smd male pin header, 5 pins [form="♂ (male)"]
  J17 = double row smd male pin header, 4 pins [form="♂ (male)"]
  J19 = double row smd male pin header, 6 pins [form="♂ (male)"]
  J20 = single row smd male pin header, 1 pin [form="♂ (male)"]  # not connected
  J21 = single row smd male pin header, 1 pin [form="♂ (male)"]  # not connected
  J22 = single row smd male pin header, 1 pin [form="♂ (male)"]  # not connected
  J23 = single row smd male pin header, 1 pin [form="♂ (male)"]  # not connected
  J15 = single row smd male pin header, 10 pins [form="♂ (male)"]  # not connected
  J14 = single row smd male pin header, 10 pins [form="♂ (male)"]  # not connected
  IC6 = IC, DIP package, 16 pins [chip_label=MCP3424]
  J24 = single row smd male pin header, 10 pins [form="♂ (male)"]
  R2 = Resistor [tolerance=±5% resistance=10k package="0402 [SMD]"]  # not connected
  J27 = single row smd male pin header, 3 pins [form="♂ (male)"]  # not connected
  J26 = single row smd male pin header, 3 pins [form="♂ (male)"]
  J25 = single row smd male pin header, 3 pins [form="♂ (male)"]  # not connected
  J30 = single row smd male pin header, 10 pins [form="♂ (male)"]
  J29 = single row smd male pin header, 5 pins [form="♂ (male)"]
  J32 = single row smd male pin header, 13 pins [form="♂ (male)"]  # not connected
  J33 = single row smd male pin header, 5 pins [form="♂ (male)"]  # not connected
  J34 = single row smd male pin header, 3 pins [form="♂ (male)"]  # not connected
  J35 = single row smd male pin header, 3 pins [form="♂ (male)"]  # not connected
  R3 = Resistor [tolerance=±5% resistance=10k package="0402 [SMD]"]  # not connected
  J36 = single row smd male pin header, 5 pins [form="♂ (male)"]  # not connected
  J37 = single row smd male pin header, 3 pins [form="♂ (male)"]  # not connected
  J38 = single row smd male pin header, 4 pins [form="♂ (male)"]  # not connected
  J31 = single row smd male pin header, 13 pins [form="♂ (male)"]  # not connected

nets:
  N1: IC1.pin4, J24.pin10
  N2: IC1.pin5, J24.pin9
  N3: IC1.pin6, IC2.pin1, IC3.pin1, J29.pin1
  N4: IC1.pin11, IC4.pin4
  N5: IC1.pin12, IC4.pin5
  N6: IC1.pin13, IC3.pin5
  N7: IC1.pin14, IC3.pin4
  N8: IC1.pin15, IC2.pin5
  N9: IC1.pin16, IC2.pin4
  N10: IC2.pin2, IC3.pin2, IC4.pin2, J26.pin1, J30.pin10, J29.pin5
  N11: IC2.pin3, IC3.pin3, IC4.pin3
  N12: IC5.pin2, J13.pin2, IC6.pin16
  N13: IC5.pin3, J13.pin3
  N14: IC5.pin4, IC8.pin2, J13.pin4
  N15: IC5.pin5, J13.pin5
  N16: IC7.pin1, J12.pin5, IC6.pin13
  N17: IC8.pin1, J19.pin2
  N18: IC8.pin4, IC6.pin9
  N19: IC8.pin5, IC6.pin10
  N20: J12.pin4, IC6.pin14
  N21: J17.pin2, J19.pin4
  N22: J17.pin3, J19.pin3
  N23: J24.pin7, J26.pin3
  N24: J24.pin8, J26.pin2

notes:
  4 x temp probe,
  Connect to board
  For MOS ICs VDD is the more positive supply voltage and Vss is the more negative supply voltage.
  connect FCL100 sync
  ALREVES
  TEMP-2------
  VCC (2)
  GND (1)
  CE0 (4) - (o -24)
  MISO (3) (y - 21)
  SCLK (5) (b-23)
  MAG
  Vcc
  5 or 3 V
  GND
  GND
  SCL (blue)
  SDA (green)
  TEMP-2------
  P1-1 Vcc
  P1-3 Vcc (17)
  P1-5 GRD
  P2-6 MOSI (o-19)
  P2-5 MISO (y - 21)
  P2-4 SCLK (b-23)
  P2-2 C1 (g 26)
