# Fritzing sketch tempSensor_pcb (saved by Fritzing 0.9.3b)
circuit board: 6.69866cm x 4.42388cm
perfboards: 1

parts:
  J5 = female pin header, 4 pins [form="♀ (female)"]
  IC2 = IC, DIP package, 10 pins [chip_label=fcl100]
  IC3 = IC, DIP package, 10 pins [chip_label=fcl100]
  J7 = female pin header, 10 pins [form="♀ (female)"]
  IC1 = IC, DIP package, 16 pins [chip_label=mcp3424]
  J8 = female pin header, 6 pins [form="♀ (female)"]
  J9 = female alternating pin header, 5 pins [form="♀ (female)"]  # not connected
  J10 = female pin header, 5 pins [form="♀ (female)"]  # not connected
  J11 = female pin header, 10 pins [form="♀ (female)"]
  J12 = female alternating pin header, 5 pins [form="♀ (female)"]

nets:
  N1: J5.pin1, IC2.pin4, IC3.pin4, J7.pin9, IC1.pin7, J8.pin1, J8.pin5, J8.pin6
  N2: J5.pin2, J5.pin3, IC1.pin2, J8.pin3, J8.pin4
  N3: J5.pin4, IC2.pin5, IC3.pin5, J7.pin10, J8.pin2
  N4: IC2.pin1, IC1.pin15
  N5: IC2.pin2, IC1.pin16
  N6: IC2.pin3, IC3.pin3, J7.pin3, J7.pin4, J7.pin5, J7.pin6, J7.pin7, J7.pin8
  N7: IC3.pin1, IC1.pin13
  N8: IC3.pin2, IC1.pin14
  N9: J7.pin1, IC1.pin10
  N10: J7.pin2, IC1.pin9
  N11: J11.pin1, J12.pin1
  N12: J11.pin2, J12.pin2
  N13: J11.pin8, J12.pin3
  N14: J11.pin9, J12.pin4
  N15: J11.pin10, J12.pin5
